# Fritzing sketch Circuit (saved by Fritzing 0.9.3b)
breadboards: 1

parts:
  5V_2 = DC Power [voltage=5]
  Fan_Relay = RELAY [package=relay-jzc]
  Heater_Relay = RELAY [package=relay-jzc]
  Netduino = Netduino Plus2
  4x20_LCD = LCD-16X2 [package=lcd-16x2]
  5V_1 = DC Power [voltage=5]
  Channel_2 = NPN-Transistor [package="TO92 [THT]"]
  LED2 = LEDs [package=led10mm]
  D1 = Diode [package=diode-1n4001]
  R1 = Resistor [tolerance=±5% resistance=150 package="1206 [SMD]"]
  Channel_3 = NPN-Transistor [package="TO92 [THT]"]
  LED3 = LEDs [package=led10mm]
  D2 = Diode [package=diode-1n4001]
  R2 = Resistor [tolerance=±5% resistance=150 package="1206 [SMD]"]
  ENCODER1 = Rotary Encoder with Knob
  T1 = LM35 Temperature Sensor [package="TO92 [THT]"]

nets:
  N1: 5V_2.V+, Fan_Relay.COIL1, D1.C
  GND: 5V_2.V-, Netduino.GND, 4x20_LCD.VSS, 4x20_LCD.VO, 4x20_LCD.R_W, 4x20_LCD.K, 5V_1.V-, Channel_2.C, Channel_3.C, ENCODER1.no_name_yet#3, T1.GND
  N2: Fan_Relay.COIL2, Channel_2.E, D1.A
  Fan +: Fan_Relay.NO
  110V Household Main: Fan_Relay.MAIN, Heater_Relay.MAIN
  N3: Heater_Relay.COIL2, Channel_3.E, D2.A
  Heater +: Heater_Relay.NO
  N4: Heater_Relay.COIL1, D2.C
  N5: Netduino.D13_SPCK, 4x20_LCD.DB7
  N6: Netduino.D12_MISO, 4x20_LCD.DB6
  N7: Netduino.D11_MOSI, 4x20_LCD.DB5
  N8: Netduino.D10_PWM3, 4x20_LCD.DB4
  N9: Netduino.D9_PWM2, 4x20_LCD.E
  N10: Netduino.D8_CTS1, 4x20_LCD.RS
  N11: Netduino.D7_RTS1, ENCODER1.no_name_yet#1
  N12: Netduino.D6_PWM1, ENCODER1.no_name_yet#2
  N13: Netduino.D5_PWM0, ENCODER1.no_name_yet#5
  N14: Netduino.D3_TX1, LED2.A
  N15: Netduino.D2_RX1, LED3.A
  N16: Netduino.3V3, ENCODER1.no_name_yet#4, T1.+Vs
  +5V: Netduino.+5V, 4x20_LCD.VDD, 4x20_LCD.A
  N17: Netduino.VIN, 5V_1.V+
  N18: Netduino.A0, T1.Vout
  N19: Channel_2.B, R1.Pin_1
  N20: LED2.C, R1.Pin_0
  N21: Channel_3.B, R2.Pin_1
  N22: LED3.C, R2.Pin_0

custom parts:
  Rotary Encoder with Knob: Rotary Encoder with 1/4" Shaft and Knob
